# Fritzing sketch Hallway_Room_Sensor (saved by Fritzing 0.8.7b)

parts:
  Raspberry_Pi_Zero1 = Raspberry Pi Zero
  PIR1 = PIR sensor

nets:
  N1: Raspberry_Pi_Zero1.GIPO23, PIR1.SIG
  GND: Raspberry_Pi_Zero1.GND, PIR1.GND
  5V: Raspberry_Pi_Zero1.5V, PIR1.VDD
